// Logisim project ISAP-1_modelA_ver1_1.circ as structural Verilog: 9 circuits, main circuit main
module main (
  input  RESET,
  input  Manual,
  input  Pulse
);

  wire addressregister_1_r, alu_1_w, CLK, clock_1_out, CP, DM, EA, EI, EP, EU, HLT, IO, ir_1_r, ir_1_w, LA,
       LAR, LB, LI, not_1_out, not_2_out, output_1_r, pc_1_w, registera_1_r, registera_1_w, registerb_1_r, SU;
  wire [3:0] addressregister_1_abus, ir_1_instr, pc_1_probe;
  wire [7:0] alu_1_probe, ir_1_probe, output_1_out, registera_1_alua, registerb_1_alub, rom_1_data;

  not not_1 (not_1_out, not_1_out);
  LED led_1 (.in(CP));
  // Probe on addressregister_1_abus
  // Probe on ir_1_instr
  ROM #(.addrWidth(4)) rom_1 (.addr(addressregister_1_abus), .data(rom_1_data), .sel(DM));
  LED led_2 (.in(DM));
  // Probe on addressregister_1_abus
  // Probe on pc_1_probe
  // Probe on pc_1_probe
  // Probe on ir_1_probe
  // Probe on ir_1_probe
  // Probe on ir_1_instr
  // Probe on rom_1_data
  // Probe on rom_1_data
  LED led_3 (.in(addressregister_1_r));
  AddressRegister addressregister_1 (
    .DIN(rom_1_data), .LAR(LAR), .CLK(CLK), .ABUS(addressregister_1_abus), .R(addressregister_1_r));
  PC pc_1 (.CP(CP), .CLK(CLK), .CLR(RESET), .EP(EP), .DOUT(rom_1_data), .PROBE(pc_1_probe), .W(pc_1_w));
  LED led_4 (.in(pc_1_w));
  LED led_5 (.in(ir_1_r));
  IR ir_1 (
    .LI(LI), .CLK(CLK), .CLR(RESET), .EI(EI), .DOUT(rom_1_data), .INSTR(ir_1_instr), .PROBE(ir_1_probe),
    .DIN(rom_1_data), .R(ir_1_r), .W(ir_1_w));
  LED led_6 (.in(ir_1_w));
  CONTROL control_1 (
    .INSTR(ir_1_instr), .CLK(CLK), .CLR(RESET), .CTRL({IO, LB, EU, SU, EA, LA, EI, LI, DM, LAR, EP, CP, HLT}));
  LED led_7 (.in(output_1_r));
  LED led_8 (.in(registera_1_r));
  LED led_9 (.in(registera_1_w));
  LED led_10 (.in(alu_1_w));
  LED led_11 (.in(registerb_1_r));
  LED led_12 (.in(output_1_out[5]));
  LED led_13 (.in(output_1_out[7]));
  LED led_14 (.in(output_1_out[4]));
  LED led_15 (.in(output_1_out[6]));
  // Probe on output_1_out
  // Probe on output_1_out
  // Probe on registera_1_alua
  // Probe on registera_1_alua
  // Probe on registerb_1_alub
  // Probe on registerb_1_alub
  LED led_16 (.in(output_1_out[0]));
  LED led_17 (.in(output_1_out[1]));
  LED led_18 (.in(output_1_out[2]));
  LED led_19 (.in(output_1_out[3]));
  OUTPUT output_1 (.DIN(rom_1_data), .IO(IO), .CLK(CLK), .OUT(output_1_out), .R(output_1_r));
  RegisterA registera_1 (
    .DIN(rom_1_data), .LA(LA), .CLK(CLK), .EA(EA), .DOUT(rom_1_data), .ALUA(registera_1_alua),
    .R(registera_1_r), .W(registera_1_w));
  ALU alu_1 (
    .ALUA(registera_1_alua), .ALUB(registerb_1_alub), .SU(SU), .EU(EU), .PROBE(alu_1_probe),
    .DOUT(rom_1_data), .W(alu_1_w));
  RegisterB registerb_1 (.DIN(rom_1_data), .LB(LB), .CLK(CLK), .ALUB(registerb_1_alub), .R(registerb_1_r));
  Clock clock_1 (.out(clock_1_out));
  // Probe on alu_1_probe
  // Probe on alu_1_probe
  not not_2 (not_2_out, HLT);
  Multiplexer #(.disabled(0)) multiplexer_1 (.in0(clock_1_out), .in1(Pulse), .out(CLK), .sel(Manual), .en(not_2_out));

  // Other names for the same wires on the sheet: CLR = RESET

  // Notes on the sheet:
  //   ISAP-1
  //   CPU
  //   MEMORY   SUBSYSTEM
  //   ROM
  //   Address Bus
  //   4 bit
  //   Opcode
  //   contents of rom_1 (hex, n*v repeats v):
  //   4 11 20 30 44 50 60 70 80 90 a0 b0 c0 d0 e0 f0
  //   Address Reg
  //   PC
  //   IR
  //   CONTROL
  //   UNIT
  //   Data Bus
  //   8 bit
  //   ISAP-1   COMPUTER   Version 1.1
  //   I/O   SUBSYSTEM
  //   OUTPUT
  //   A
  //   ALU
  //   B
  //   Control Bus
  //   5 bit
  //   CONTROL   PANEL
  //   out
  //   out
  //   out
  //   in
  //   in
endmodule

module RegisterA (
  input  [7:0] DIN,
  input  LA,
  input  CLK,
  input  EA,
  output [7:0] ALUA,
  output [7:0] DOUT,
  output R,
  output W
);

  Register register_1 (.D(DIN), .en(LA), .Q(ALUA), .clk(CLK));  // open: clr
  assign DOUT = EA ? ALUA : 8'bz;  // Controlled_Buffer controlled_buffer_1

  assign R = LA;
  assign W = EA;

  // Notes on the sheet:
  //   8 bit Register
  //   ACCUMULATOR  REGISTER
  //   8 bit Buffer
endmodule

module AddressRegister (
  input  [7:0] DIN,
  input  LAR,
  input  CLK,
  output [3:0] ABUS,
  output R
);

  Register #(.width(4)) register_1 (.D(DIN[3:0]), .en(LAR), .Q(ABUS), .clk(CLK));  // open: clr

  assign R = LAR;

  // Notes on the sheet:
  //   4 bit Register
  //   ADDRESS REGISTER
endmodule

module PC (
  input  CP,
  input  CLK,
  input  CLR,
  input  EP,
  output [3:0] PROBE,
  output [7:0] DOUT,
  output W
);

  wire j_k_ff_1_qn, j_k_ff_2_qn, j_k_ff_3_qn, j_k_ff_4_qn;

  J_K_Flip_Flop j_k_ff_1 (.J(CP), .clk(CLK), .K(CP), .Q(PROBE[0]), .Qn(j_k_ff_1_qn), .reset(CLR));  // open: preset, en
  assign DOUT[0] = EP ? PROBE[0] : 1'bz;  // Controlled_Buffer controlled_buffer_1
  J_K_Flip_Flop j_k_ff_2 (
    .J(CP), .clk(j_k_ff_1_qn), .K(CP), .Q(PROBE[1]), .Qn(j_k_ff_2_qn), .reset(CLR));  // open: preset, en
  assign DOUT[1] = EP ? PROBE[1] : 1'bz;  // Controlled_Buffer controlled_buffer_2
  J_K_Flip_Flop j_k_ff_3 (
    .J(CP), .clk(j_k_ff_2_qn), .K(CP), .Q(PROBE[2]), .Qn(j_k_ff_3_qn), .reset(CLR));  // open: preset, en
  assign DOUT[2] = EP ? PROBE[2] : 1'bz;  // Controlled_Buffer controlled_buffer_3
  J_K_Flip_Flop j_k_ff_4 (
    .J(CP), .clk(j_k_ff_3_qn), .K(CP), .Q(PROBE[3]), .Qn(j_k_ff_4_qn), .reset(CLR));  // open: preset, en
  assign DOUT[3] = EP ? PROBE[3] : 1'bz;  // Controlled_Buffer controlled_buffer_4
  assign DOUT[7] = EP ? 1'b1 : 1'bz;  // Controlled_Buffer controlled_buffer_5

  assign DOUT[6:4] = {3{DOUT[7]}};
  assign W = EP;

  // Notes on the sheet:
  //   4 x JK Flip-Flop
  //   4 bit Buffer
  //   PROGRAM  COUNTER
endmodule

module IR (
  input  [7:0] DIN,
  input  LI,
  input  CLK,
  input  CLR,
  input  EI,
  output [7:0] PROBE,
  output [7:0] DOUT,
  output [3:0] INSTR,
  output R,
  output W
);

  Register register_1 (.D(DIN), .en(LI), .Q({INSTR, PROBE[3:0]}), .clk(CLK), .clr(CLR));
  assign DOUT = EI ? {4'b1111, PROBE[3:0]} : 8'bz;  // Controlled_Buffer controlled_buffer_1

  assign PROBE[7:4] = INSTR;
  assign R = LI;
  assign W = EI;

  // Notes on the sheet:
  //   8 bit Register
  //   INSTRUCTION  REGISTER
  //   8 bit Buffer
endmodule

module CONTROL (
  input  CLK,
  input  CLR,
  input  [3:0] INSTR,
  output [12:0] CTRL
);

  wire j_k_ff_1_q, j_k_ff_1_qn, j_k_ff_2_q, j_k_ff_2_qn, j_k_ff_3_q, j_k_ff_3_qn, j_k_ff_4_q, j_k_ff_4_qn,
       j_k_ff_5_q, j_k_ff_5_qn, j_k_ff_6_q, j_k_ff_6_qn, nand_1_out, nand_2_out, nand_3_out, nand_4_out,
       nand_5_out, nand_6_out, nand_7_out, nand_9_out, nand_10_out, nand_11_out, nand_13_out, nand_14_out,
       nand_15_out, nand_17_out, nand_18_out, nand_19_out, nand_20_out, nand_22_out, nand_23_out,
       nand_24_out, nand_26_out, nand_27_out, nand_28_out, nand_30_out, nor_1_out, not_1_out, not_2_out,
       not_3_out, not_4_out, not_5_out, not_6_out, not_7_out, not_8_out, not_9_out, not_11_out, not_12_out,
       or_1_out;

  not not_1 (not_1_out, INSTR[3]);
  not not_2 (not_2_out, CLK);
  not not_3 (not_3_out, INSTR[2]);
  not not_4 (not_4_out, INSTR[1]);
  not not_5 (not_5_out, INSTR[0]);
  nand nand_1 (nand_1_out, not_1_out, not_3_out, not_4_out, not_5_out);
  nand nand_2 (nand_2_out, not_1_out, not_3_out, not_4_out, INSTR[0]);
  nand nand_3 (nand_3_out, not_1_out, not_3_out, INSTR[1], not_5_out);
  nand nand_4 (nand_4_out, INSTR[3], INSTR[2], INSTR[1], not_5_out);
  nand nand_5 (nand_5_out, INSTR[3], INSTR[2], INSTR[1], INSTR[0]);
  or or_1 (or_1_out, CLR, nor_1_out);
  not not_6 (not_6_out, nand_1_out);
  not not_7 (not_7_out, nand_2_out);
  not not_8 (not_8_out, nand_3_out);
  not not_9 (not_9_out, nand_4_out);
  not not_10 (CTRL[0], nand_5_out);
  not not_11 (not_11_out, j_k_ff_1_qn);
  buf buffer_1 (CTRL[1], j_k_ff_2_q);
  buf buffer_2 (CTRL[2], j_k_ff_1_qn);
  nand nand_6 (nand_6_out, not_7_out, j_k_ff_4_q);
  nand nand_7 (nand_7_out, not_6_out, j_k_ff_4_q);
  nand nand_8 (CTRL[3], not_11_out, nand_7_out, nand_6_out, nand_9_out);
  not not_12 (not_12_out, j_k_ff_3_q);
  nand nand_9 (nand_9_out, not_8_out, j_k_ff_4_q);
  J_K_Flip_Flop j_k_ff_1 (
    .J(j_k_ff_6_qn), .clk(not_2_out), .K(j_k_ff_6_q), .Q(j_k_ff_1_q), .Qn(j_k_ff_1_qn), .reset(or_1_out));  // open: preset, en
  nand nand_10 (nand_10_out, not_7_out, j_k_ff_5_q);
  nand nand_11 (nand_11_out, not_6_out, j_k_ff_5_q);
  nand nand_12 (CTRL[4], not_12_out, nand_11_out, nand_10_out, nand_13_out);
  J_K_Flip_Flop j_k_ff_2 (
    .J(j_k_ff_1_qn), .clk(not_2_out), .K(j_k_ff_1_q), .Q(j_k_ff_2_q), .Qn(j_k_ff_2_qn), .reset(or_1_out));  // open: preset, en
  nand nand_13 (nand_13_out, not_8_out, j_k_ff_5_q);
  buf buffer_3 (CTRL[5], j_k_ff_3_q);
  J_K_Flip_Flop j_k_ff_3 (
    .J(j_k_ff_2_q), .clk(not_2_out), .K(j_k_ff_2_qn), .Q(j_k_ff_3_q), .Qn(j_k_ff_3_qn), .reset(or_1_out));  // open: preset, en
  nand nand_14 (nand_14_out, not_7_out, j_k_ff_4_q);
  nand nand_15 (nand_15_out, not_6_out, j_k_ff_4_q);
  nand nand_16 (CTRL[6], nand_15_out, nand_14_out, nand_17_out);
  J_K_Flip_Flop j_k_ff_4 (
    .J(j_k_ff_3_q), .clk(not_2_out), .K(j_k_ff_3_qn), .Q(j_k_ff_4_q), .Qn(j_k_ff_4_qn), .reset(or_1_out));  // open: preset, en
  nand nand_17 (nand_17_out, not_8_out, j_k_ff_4_q);
  nand nand_18 (nand_18_out, not_6_out, j_k_ff_5_q);
  J_K_Flip_Flop j_k_ff_5 (
    .J(j_k_ff_4_q), .clk(not_2_out), .K(j_k_ff_4_qn), .Q(j_k_ff_5_q), .Qn(j_k_ff_5_qn), .reset(or_1_out));  // open: preset, en
  nand nand_19 (nand_19_out, not_7_out, j_k_ff_6_q);
  nand nand_20 (nand_20_out, not_8_out, j_k_ff_6_q);
  nand nand_21 (CTRL[7], nand_18_out, nand_19_out, nand_20_out);
  J_K_Flip_Flop j_k_ff_6 (
    .J(j_k_ff_5_q), .clk(not_2_out), .K(j_k_ff_5_qn), .Q(j_k_ff_6_q), .Qn(j_k_ff_6_qn), .reset(or_1_out));  // open: preset, en
  nand nand_22 (nand_22_out, not_9_out, j_k_ff_4_q);
  nand nand_23 (nand_23_out, not_8_out, j_k_ff_6_q);
  not not_13 (CTRL[8], nand_22_out);
  not not_14 (CTRL[9], nand_23_out);
  nand nand_24 (nand_24_out, not_7_out, j_k_ff_6_q);
  nand nand_25 (CTRL[10], nand_24_out, nand_27_out);
  nand nand_26 (nand_26_out, not_7_out, j_k_ff_5_q);
  nand nand_27 (nand_27_out, not_8_out, j_k_ff_6_q);
  nand nand_28 (nand_28_out, not_8_out, j_k_ff_5_q);
  nand nand_29 (CTRL[11], nand_26_out, nand_28_out);
  nand nand_30 (nand_30_out, not_9_out, j_k_ff_4_q);
  not not_15 (CTRL[12], nand_30_out);
  nor nor_1 (nor_1_out, CTRL[1], CTRL[2], CTRL[3], CTRL[4], CTRL[5], CTRL[6], CTRL[7], CTRL[8], CTRL[9], CTRL[10], CTRL[11], CTRL[12]);

  // Notes on the sheet:
  //   I7
  //   /I6
  //   I6
  //   /I7
  //   I5
  //   /I5
  //   /I4
  //   I4
  //   INSTRUCTION  DECODER
  //   HLT
  //   LDA
  //   ADD
  //   SUB
  //   OUT
  //   HLT
  //   EP
  //   CP
  //   (#LM)
  //   #LAR
  //   T1
  //   #PM
  //   T2
  //   #LI
  //   RING COUNTER
  //   #EI
  //   T3
  //   CONTROL    MATRIX
  //   T4
  //   #LA
  //   T5
  //   SU
  //   EA
  //   T6
  //   EU
  //   #LB
  //   #IO
endmodule

module RegisterB (
  input  [7:0] DIN,
  input  LB,
  input  CLK,
  output [7:0] ALUB,
  output R
);

  Register register_1 (.D(DIN), .en(LB), .Q(ALUB), .clk(CLK));  // open: clr

  assign R = LB;

  // Notes on the sheet:
  //   8 bit Register
  //   REGISTER  B
endmodule

module ALU (
  input  [7:0] ALUA,
  input  [7:0] ALUB,
  input  EU,
  input  SU,
  output [7:0] PROBE,
  output [7:0] DOUT,
  output W
);

  wire [7:0] xor_1_out;

  assign xor_1_out = ALUB ^ {8{SU}};  // XOR_Gate xor_1, 8 bits wide
  Adder adder_1 (.a(ALUA), .b(xor_1_out), .out(PROBE), .cin(SU));  // open: cout
  assign DOUT = EU ? PROBE : 8'bz;  // Controlled_Buffer controlled_buffer_1

  assign W = EU;

  // Notes on the sheet:
  //   8 x XOR Gates
  //   8 bit Full Adder
  //   ALU
  //   8 bit Buffer
endmodule

module OUTPUT (
  input  [7:0] DIN,
  input  IO,
  input  CLK,
  output [7:0] OUT,
  output R
);

  Register register_1 (.D(DIN), .en(IO), .Q(OUT), .clk(CLK));  // open: clr

  assign R = IO;

  // Notes on the sheet:
  //   8 bit Register
  //   OUTPUT  REGISTER
endmodule
