// Logisim project ISAP-1_modelB_ver1_1.circ as structural Verilog: 9 circuits, main circuit main
module main (
  input  RESET,
  input  Manual,
  input  Pulse
);

  wire addressregister_1_r, alu_1_w, CLK, clock_1_out, CP, DM, EA, EI, EP, EU, HLT, IO, ir_1_r, ir_1_w, LA,
       LAR, LB, LI, not_1_out, not_2_out, output_1_r, pc_1_w, registera_1_r, registera_1_w, registerb_1_r, SU;
  wire [3:0] addressregister_1_abus, ir_1_instr, pc_1_probe;
  wire [7:0] alu_1_probe, ir_1_probe, output_1_out, registera_1_alua, registerb_1_alub, rom_1_data;

  not not_1 (not_1_out, not_1_out);
  LED led_1 (.in(CP));
  // Probe on addressregister_1_abus
  // Probe on ir_1_instr
  ROM #(.addrWidth(4)) rom_1 (.addr(addressregister_1_abus), .data(rom_1_data), .sel(DM));
  // Probe on addressregister_1_abus
  // Probe on pc_1_probe
  // Probe on pc_1_probe
  // Probe on ir_1_probe
  // Probe on ir_1_probe
  // Probe on ir_1_instr
  // Probe on rom_1_data
  // Probe on rom_1_data
  LED led_2 (.in(DM));
  LED led_3 (.in(addressregister_1_r));
  AddressRegister addressregister_1 (
    .DIN(rom_1_data), .LAR(LAR), .CLK(CLK), .ABUS(addressregister_1_abus), .R(addressregister_1_r));
  PC pc_1 (.CP(CP), .CLK(CLK), .CLR(RESET), .EP(EP), .DOUT(rom_1_data), .PROBE(pc_1_probe), .W(pc_1_w));
  LED led_4 (.in(pc_1_w));
  LED led_5 (.in(ir_1_r));
  IR ir_1 (
    .LI(LI), .CLK(CLK), .CLR(RESET), .EI(EI), .DOUT(rom_1_data), .INSTR(ir_1_instr), .PROBE(ir_1_probe),
    .DIN(rom_1_data), .R(ir_1_r), .W(ir_1_w));
  LED led_6 (.in(ir_1_w));
  CONTROL control_1 (
    .INSTR(ir_1_instr), .CLK(CLK), .CLR(RESET), .CTRL({IO, LB, EU, SU, EA, LA, EI, LI, DM, LAR, EP, CP, HLT}));
  LED led_7 (.in(output_1_r));
  LED led_8 (.in(registera_1_r));
  LED led_9 (.in(registera_1_w));
  LED led_10 (.in(alu_1_w));
  LED led_11 (.in(registerb_1_r));
  LED led_12 (.in(output_1_out[6]));
  LED led_13 (.in(output_1_out[5]));
  LED led_14 (.in(output_1_out[7]));
  LED led_15 (.in(output_1_out[4]));
  // Probe on output_1_out
  // Probe on output_1_out
  // Probe on registera_1_alua
  // Probe on registera_1_alua
  // Probe on registerb_1_alub
  // Probe on registerb_1_alub
  LED led_16 (.in(output_1_out[0]));
  LED led_17 (.in(output_1_out[2]));
  LED led_18 (.in(output_1_out[3]));
  LED led_19 (.in(output_1_out[1]));
  OUTPUT output_1 (.DIN(rom_1_data), .IO(IO), .CLK(CLK), .OUT(output_1_out), .R(output_1_r));
  RegisterA registera_1 (
    .DIN(rom_1_data), .LA(LA), .CLK(CLK), .EA(EA), .DOUT(rom_1_data), .ALUA(registera_1_alua),
    .R(registera_1_r), .W(registera_1_w));
  ALU alu_1 (
    .ALUA(registera_1_alua), .ALUB(registerb_1_alub), .SU(SU), .EU(EU), .PROBE(alu_1_probe),
    .DOUT(rom_1_data), .W(alu_1_w));
  RegisterB registerb_1 (.DIN(rom_1_data), .LB(LB), .CLK(CLK), .ALUB(registerb_1_alub), .R(registerb_1_r));
  Clock clock_1 (.out(clock_1_out));
  // Probe on alu_1_probe
  // Probe on alu_1_probe
  not not_2 (not_2_out, HLT);
  Multiplexer #(.disabled(0)) multiplexer_1 (.in0(clock_1_out), .in1(Pulse), .out(CLK), .sel(Manual), .en(not_2_out));

  // Other names for the same wires on the sheet: CLR = RESET

  // Notes on the sheet:
  //   ISAP-1
  //   CPU
  //   MEMORY   SUBSYSTEM
  //   ROM
  //   Address Bus
  //   4 bit
  //   Opcode
  //   contents of rom_1 (hex, n*v repeats v):
  //   9 1a 1b 2c e0 f0 ff ff ff 10 14 18 20 ff ff ff
  //   Address Reg
  //   PC
  //   IR
  //   CONTROL
  //   UNIT
  //   Data Bus
  //   8 bit
  //   ISAP-1   COMPUTER   Version 1.1
  //   I/O   SUBSYSTEM
  //   OUTPUT
  //   A
  //   ALU
  //   B
  //   Control Bus
  //   5 bit
  //   CONTROL   PANEL
  //   out
  //   out
  //   out
  //   in
  //   in
endmodule

module RegisterA (
  input  [7:0] DIN,
  input  LA,
  input  CLK,
  input  EA,
  output [7:0] ALUA,
  output [7:0] DOUT,
  output R,
  output W
);

  Register register_1 (.D(DIN), .en(LA), .Q(ALUA), .clk(CLK));  // open: clr
  assign DOUT = EA ? ALUA : 8'bz;  // Controlled_Buffer controlled_buffer_1

  assign R = LA;
  assign W = EA;

  // Notes on the sheet:
  //   8 bit Register
  //   ACCUMULATOR  REGISTER
  //   8 bit Buffer
endmodule

module AddressRegister (
  input  [7:0] DIN,
  input  LAR,
  input  CLK,
  output [3:0] ABUS,
  output R
);

  Register #(.width(4)) register_1 (.D(DIN[3:0]), .en(LAR), .Q(ABUS), .clk(CLK));  // open: clr

  assign R = LAR;

  // Notes on the sheet:
  //   4 bit Register
  //   ADDRESS REGISTER
endmodule

module PC (
  input  CP,
  input  CLK,
  input  CLR,
  input  EP,
  output [3:0] PROBE,
  output [7:0] DOUT,
  output W
);

  wire j_k_ff_1_qn, j_k_ff_2_qn, j_k_ff_3_qn, j_k_ff_4_qn;

  J_K_Flip_Flop j_k_ff_1 (.J(CP), .clk(CLK), .K(CP), .Q(PROBE[0]), .Qn(j_k_ff_1_qn), .reset(CLR));  // open: preset, en
  assign DOUT[0] = EP ? PROBE[0] : 1'bz;  // Controlled_Buffer controlled_buffer_1
  J_K_Flip_Flop j_k_ff_2 (
    .J(CP), .clk(j_k_ff_1_qn), .K(CP), .Q(PROBE[1]), .Qn(j_k_ff_2_qn), .reset(CLR));  // open: preset, en
  assign DOUT[1] = EP ? PROBE[1] : 1'bz;  // Controlled_Buffer controlled_buffer_2
  J_K_Flip_Flop j_k_ff_3 (
    .J(CP), .clk(j_k_ff_2_qn), .K(CP), .Q(PROBE[2]), .Qn(j_k_ff_3_qn), .reset(CLR));  // open: preset, en
  assign DOUT[2] = EP ? PROBE[2] : 1'bz;  // Controlled_Buffer controlled_buffer_3
  J_K_Flip_Flop j_k_ff_4 (
    .J(CP), .clk(j_k_ff_3_qn), .K(CP), .Q(PROBE[3]), .Qn(j_k_ff_4_qn), .reset(CLR));  // open: preset, en
  assign DOUT[3] = EP ? PROBE[3] : 1'bz;  // Controlled_Buffer controlled_buffer_4
  assign DOUT[7] = EP ? 1'b1 : 1'bz;  // Controlled_Buffer controlled_buffer_5

  assign DOUT[6:4] = {3{DOUT[7]}};
  assign W = EP;

  // Notes on the sheet:
  //   4 x JK Flip-Flop
  //   4 bit Buffer
  //   PROGRAM  COUNTER
endmodule

module IR (
  input  [7:0] DIN,
  input  LI,
  input  CLK,
  input  CLR,
  input  EI,
  output [7:0] PROBE,
  output [7:0] DOUT,
  output [3:0] INSTR,
  output R,
  output W
);

  Register register_1 (.D(DIN), .en(LI), .Q({INSTR, PROBE[3:0]}), .clk(CLK), .clr(CLR));
  assign DOUT = EI ? {4'b1111, PROBE[3:0]} : 8'bz;  // Controlled_Buffer controlled_buffer_1

  assign PROBE[7:4] = INSTR;
  assign R = LI;
  assign W = EI;

  // Notes on the sheet:
  //   8 bit Register
  //   INSTRUCTION  REGISTER
  //   8 bit Buffer
endmodule

module CONTROL (
  input  CLK,
  input  CLR,
  input  [3:0] INSTR,
  output [12:0] CTRL
);

  wire and_1_out, and_2_out, j_k_ff_1_q, j_k_ff_1_qn, j_k_ff_2_q, j_k_ff_2_qn, j_k_ff_3_q, j_k_ff_3_qn,
       j_k_ff_4_q, j_k_ff_4_qn, j_k_ff_5_q, j_k_ff_5_qn, j_k_ff_6_q, j_k_ff_6_qn, nand_1_out, nand_2_out,
       not_1_out, not_3_out, not_4_out, not_5_out, not_6_out, not_8_out, not_15_out, not_16_out, not_17_out,
       not_18_out, not_19_out, or_1_out;
  wire [3:0] counter_1_q, rom_1_data;
  wire [9:0] rom_2_data;

  not not_1 (not_1_out, CLK);
  // Probe on rom_1_data
  nand nand_1 (nand_1_out, INSTR[3], INSTR[2], INSTR[1], INSTR[0]);
  ROM #(.addrWidth(4), .dataWidth(4)) rom_1 (.addr(INSTR), .data(rom_1_data));  // open: sel
  not not_2 (CTRL[0], nand_1_out);
  not not_3 (not_3_out, nand_2_out);
  not not_4 (not_4_out, j_k_ff_3_q);
  or or_1 (or_1_out, CLR, j_k_ff_1_qn);
  and and_1 (and_1_out, CLR, not_3_out);
  Counter #(.width(4), .max('hf)) counter_1 (
    .load(j_k_ff_3_q), .D(rom_1_data), .count(not_4_out), .Q(counter_1_q), .clk(not_1_out), .clr(and_2_out));  // open: carry
  not not_5 (not_5_out, not_6_out);
  not not_6 (not_6_out, or_1_out);
  not not_7 (CTRL[3], rom_2_data[9]);
  // Probe on counter_1_q
  and and_2 (and_2_out, or_1_out, not_8_out);
  not not_8 (not_8_out, not_5_out);
  J_K_Flip_Flop j_k_ff_1 (
    .J(j_k_ff_6_qn), .clk(not_1_out), .K(j_k_ff_6_q), .Q(j_k_ff_1_q), .Qn(j_k_ff_1_qn), .reset(and_1_out));  // open: preset, en
  not not_9 (CTRL[4], rom_2_data[8]);
  J_K_Flip_Flop j_k_ff_2 (
    .J(j_k_ff_1_qn), .clk(not_1_out), .K(j_k_ff_1_q), .Q(j_k_ff_2_q), .Qn(j_k_ff_2_qn), .reset(and_1_out));  // open: preset, en
  not not_10 (CTRL[5], rom_2_data[7]);
  J_K_Flip_Flop j_k_ff_3 (
    .J(j_k_ff_2_q), .clk(not_1_out), .K(j_k_ff_2_qn), .Q(j_k_ff_3_q), .Qn(j_k_ff_3_qn), .reset(and_1_out));  // open: preset, en
  not not_11 (CTRL[6], rom_2_data[6]);
  J_K_Flip_Flop j_k_ff_4 (
    .J(j_k_ff_3_q), .clk(not_1_out), .K(j_k_ff_3_qn), .Q(j_k_ff_4_q), .Qn(j_k_ff_4_qn), .reset(and_1_out));  // open: preset, en
  ROM #(.addrWidth(4), .dataWidth(12)) rom_2 (
    .addr(counter_1_q),
    .data({CTRL[1], CTRL[2], rom_2_data[9:5], CTRL[8], CTRL[9], CTRL[10], rom_2_data[1:0]}));  // open: sel
  not not_12 (CTRL[7], rom_2_data[5]);
  J_K_Flip_Flop j_k_ff_5 (
    .J(j_k_ff_4_q), .clk(not_1_out), .K(j_k_ff_4_qn), .Q(j_k_ff_5_q), .Qn(j_k_ff_5_qn), .reset(and_1_out));  // open: preset, en
  // Probe on {CTRL[1], CTRL[2], rom_2_data[9:5], CTRL[8], CTRL[9], CTRL[10], rom_2_data[1:0]}
  // Probe on {CTRL[1], CTRL[2], rom_2_data[9:5], CTRL[8], CTRL[9], CTRL[10], rom_2_data[1:0]}
  J_K_Flip_Flop j_k_ff_6 (
    .J(j_k_ff_5_q), .clk(not_1_out), .K(j_k_ff_5_qn), .Q(j_k_ff_6_q), .Qn(j_k_ff_6_qn), .reset(and_1_out));  // open: preset, en
  not not_13 (CTRL[11], rom_2_data[1]);
  not not_14 (CTRL[12], rom_2_data[0]);
  not not_15 (not_15_out, CTRL[1]);
  not not_16 (not_16_out, CTRL[2]);
  not not_17 (not_17_out, CTRL[8]);
  not not_18 (not_18_out, CTRL[9]);
  not not_19 (not_19_out, CTRL[10]);
  nand nand_2 (nand_2_out, not_15_out, not_16_out, rom_2_data[9], rom_2_data[8], rom_2_data[7], rom_2_data[6], rom_2_data[5], not_17_out, not_18_out, not_19_out, rom_2_data[1], rom_2_data[0]);

  // Notes on the sheet:
  //   I7
  //   I6
  //   I5
  //   I4
  //   INSTRUCTION  DECODER
  //   Address ROM
  //   16 X 4
  //   HLT
  //   contents of rom_1 (hex, n*v repeats v):
  //   3 6 9 11*f c f
  //   HLT
  //   CP
  //   EP
  //   LAR
  //   (LM)
  //   T1
  //   PM
  //   (CE)
  //   T2
  //   LI
  //   RING COUNTER
  //   Control ROM
  //   16 x 12
  //   EI
  //   T3
  //   contents of rom_2 (hex, n*v repeats v):
  //   5e3 be3 263 1a3 2c3 3e3 1a3 2e1 3c7 1a3 2e1 3cf 3f2 3e3 3e3 fff
  //   LA
  //   T4
  //   EA
  //   T5
  //   EU
  //   SU
  //   LB
  //   IO
  //   T6
  //   (LO)
endmodule

module RegisterB (
  input  [7:0] DIN,
  input  LB,
  input  CLK,
  output [7:0] ALUB,
  output R
);

  Register register_1 (.D(DIN), .en(LB), .Q(ALUB), .clk(CLK));  // open: clr

  assign R = LB;

  // Notes on the sheet:
  //   8 bit Register
  //   REGISTER  B
endmodule

module ALU (
  input  [7:0] ALUA,
  input  [7:0] ALUB,
  input  EU,
  input  SU,
  output [7:0] PROBE,
  output [7:0] DOUT,
  output W
);

  wire [7:0] xor_1_out;

  assign xor_1_out = ALUB ^ {8{SU}};  // XOR_Gate xor_1, 8 bits wide
  Adder adder_1 (.a(ALUA), .b(xor_1_out), .out(PROBE), .cin(SU));  // open: cout
  assign DOUT = EU ? PROBE : 8'bz;  // Controlled_Buffer controlled_buffer_1

  assign W = EU;

  // Notes on the sheet:
  //   8 x XOR Gates
  //   8 bit Full Adder
  //   ALU
  //   8 bit Buffer
endmodule

module OUTPUT (
  input  [7:0] DIN,
  input  IO,
  input  CLK,
  output [7:0] OUT,
  output R
);

  Register register_1 (.D(DIN), .en(IO), .Q(OUT), .clk(CLK));  // open: clr

  assign R = IO;

  // Notes on the sheet:
  //   8 bit Register
  //   OUTPUT  REGISTER
endmodule
