// Logisim project ISAP-1_v1.circ as structural Verilog: 5 circuits, main circuit main
module main (
  input  RESET,
  input  Manual,
  input  Pulse
);

  wire addressregister_1_r, CLK, clock_1_out, CP, EI, EP, ir_1_r, ir_1_w, LAR, LI, LP, pc_1_r, pc_1_w, PM;
  wire [3:0] addressregister_1_abus, ir_1_instr;
  wire [7:0] ir_1_probe, pc_1_probe, rom_1_data;

  CONTROL control_1 (.INSTR(ir_1_instr), .CTRL({EI, LP, LI, PM, CP, LAR, EP}), .CLK(CLK), .CLR(RESET));
  // Probe on addressregister_1_abus
  // Probe on pc_1_probe
  // Probe on ir_1_probe
  // Probe on ir_1_instr
  // Probe on {EI, LP, LI, PM, CP, LAR, EP}
  ROM #(.addrWidth(4)) rom_1 (.addr(addressregister_1_abus), .data(rom_1_data), .sel(PM));
  LED led_1 (.in(PM));
  LED led_2 (.in(addressregister_1_r));
  AddressRegister addressregister_1 (
    .DIN(rom_1_data), .LAR(LAR), .CLK(CLK), .ABUS(addressregister_1_abus), .R(addressregister_1_r));
  LED led_3 (.in(pc_1_r));
  PC pc_1 (
    .LP(LP), .DIN(rom_1_data), .CP(CP), .CLK(CLK), .CLR(RESET), .EP(EP), .DOUT(rom_1_data),
    .PROBE(pc_1_probe), .W(pc_1_w), .R(pc_1_r));
  LED led_4 (.in(pc_1_w));
  LED led_5 (.in(ir_1_r));
  IR ir_1 (
    .LI(LI), .CLK(CLK), .CLR(RESET), .EI(EI), .DOUT(rom_1_data), .INSTR(ir_1_instr), .PROBE(ir_1_probe),
    .DIN(rom_1_data), .R(ir_1_r), .W(ir_1_w));
  LED led_6 (.in(ir_1_w));
  // Probe on rom_1_data
  Clock clock_1 (.out(clock_1_out));
  Multiplexer multiplexer_1 (.in0(clock_1_out), .in1(Pulse), .out(CLK), .sel(Manual));  // open: en

  // Other names for the same wires on the sheet: CLR = RESET

  // Notes on the sheet:
  //   Control Bus
  //   ISAP-1
  //   CPU
  //   MEMORY SUBSYSTEM
  //   ROM
  //   Address Bus
  //   Address Reg
  //   PC
  //   IR
  //   Opcode
  //   CONTROL
  //   UNIT
  //   contents of rom_1 (hex, n*v repeats v):
  //   5 16 1 2 0 7 8
  //   Data Bus
  //   CONTROL PANEL
endmodule

module AddressRegister (
  input  [7:0] DIN,
  input  LAR,
  input  CLK,
  output [3:0] ABUS,
  output R
);

  Register #(.width(4)) register_1 (.D(DIN[3:0]), .en(LAR), .Q(ABUS), .clk(CLK));  // open: clr

  assign R = LAR;
endmodule

module PC (
  input  LP,
  input  [7:0] DIN,
  input  CP,
  input  CLK,
  input  CLR,
  input  EP,
  output [7:0] PROBE,
  output [7:0] DOUT,
  output W,
  output R
);

  // Probe on PROBE[3:0]
  Counter #(.width(4), .max('hf)) counter_1 (
    .load(LP), .D(DIN[3:0]), .count(CP), .Q(PROBE[3:0]), .clk(CLK), .clr(CLR));  // open: carry
  assign PROBE[7:4] = 4'b0000;  // Buffer buffer_1, 4 bits wide
  assign DOUT = EP ? PROBE : 8'bz;  // Controlled_Buffer controlled_buffer_1
  // Probe on PROBE[7:4]
  // Probe on DOUT

  assign R = LP;
  assign W = EP;
endmodule

module IR (
  input  [7:0] DIN,
  input  LI,
  input  CLK,
  input  CLR,
  input  EI,
  output [7:0] PROBE,
  output [7:0] DOUT,
  output [3:0] INSTR,
  output R,
  output W
);

  Register register_1 (.D(DIN), .en(LI), .Q({INSTR, PROBE[3:0]}), .clk(CLK), .clr(CLR));
  // Probe on PROBE[3:0]
  assign DOUT[3:0] = EI ? PROBE[3:0] : 4'bz;  // Controlled_Buffer controlled_buffer_1
  assign DOUT[7:4] = EI ? PROBE[3:0] : 4'bz;  // Controlled_Buffer controlled_buffer_2
  // Probe on DOUT[3:0]
  // Probe on DOUT[7:4]

  assign PROBE[7:4] = INSTR;
  assign R = LI;
  assign W = EI;
endmodule

module CONTROL (
  input  [3:0] INSTR,
  input  CLK,
  input  CLR,
  output [6:0] CTRL
);

  wire decoder_1_out0, decoder_1_out1, decoder_1_out2, not_1_out, or_1_out;
  wire [2:0] counter_1_q;

  not not_1 (not_1_out, CLK);
  // Probe on counter_1_q
  Counter #(.width(3), .max('h7)) counter_1 (
    .Q(counter_1_q), .clk(not_1_out), .clr(or_1_out));  // open: load, D, count, carry
  or or_1 (or_1_out, CLR, decoder_1_out2);
  Decoder #(.select(3), .disabled(0), .enable("false")) decoder_1 (
    .out0(decoder_1_out0), .out1(decoder_1_out1), .out2(decoder_1_out2), .sel(counter_1_q));  // open: out3, out4, out5, out6, out7
  buf buffer_1 (CTRL[0], decoder_1_out0);
  buf buffer_2 (CTRL[1], decoder_1_out0);
  buf buffer_3 (CTRL[2], decoder_1_out1);
  buf buffer_4 (CTRL[3], decoder_1_out1);
  buf buffer_5 (CTRL[4], decoder_1_out1);

  assign CTRL[6:5] = 2'b00;

  // Notes on the sheet:
  //   Step Counter
  //   NEXT
  //   Step Decoder
  //   T1
  //   T7
  //   EP
  //   LAR
  //   CP
  //   PM
  //   LI
  //   LP
  //   EI
endmodule
