// Logisim project ISAP-1_v4.circ as structural Verilog: 7 circuits, main circuit main
module main (
  input  in_1,
  input  RESET,
  input  Manual,
  input  Pulse
);

  wire addressregister_1_r, CLK, clock_1_out, CP, DM, EA, EI, EP, ir_1_r, ir_1_w, LAH, LAL, LAR, LI, LP,
       pc_1_r, pc_1_w, PM, registera_1_r, registera_1_w, W;
  wire [3:0] addressregister_1_abus, ir_1_instr;
  wire [7:0] ir_1_probe, pc_1_probe, registera_1_alua, rom_1_data;

  CONTROL control_1 (
    .INSTR(ir_1_instr), .CTRL(CP), .CLK(CLK), .CLR(RESET), .CTRL_R({W, LAH, LAL, LP, LI, LAR}),
    .CTRL_W({DM, EA, EI, PM, EP}));
  // Probe on addressregister_1_abus
  // Probe on pc_1_probe
  // Probe on ir_1_probe
  // Probe on ir_1_instr
  ROM #(.addrWidth(4)) rom_1 (.addr(addressregister_1_abus), .data(rom_1_data), .sel(PM));
  LED led_1 (.in(PM));
  RAM #(.addrWidth(4), .bus("asynch")) ram_1 (
    .addr(addressregister_1_abus), .data(rom_1_data), .sel(W), .ld(DM), .clr(in_1));
  LED led_2 (.in(W));
  AddressRegister addressregister_1 (
    .DIN(rom_1_data), .LAR(LAR), .CLK(CLK), .ABUS(addressregister_1_abus), .R(addressregister_1_r));
  PC pc_1 (
    .LP(LP), .DIN(rom_1_data), .CP(CP), .CLK(CLK), .CLR(RESET), .EP(EP), .DOUT(rom_1_data),
    .PROBE(pc_1_probe), .W(pc_1_w), .R(pc_1_r));
  IR ir_1 (
    .LI(LI), .CLK(CLK), .CLR(RESET), .EI(EI), .DOUT(rom_1_data), .INSTR(ir_1_instr), .PROBE(ir_1_probe),
    .DIN(rom_1_data), .R(ir_1_r), .W(ir_1_w));
  // Probe on rom_1_data
  LED led_3 (.in(addressregister_1_r));
  LED led_4 (.in(pc_1_r));
  LED led_5 (.in(pc_1_w));
  LED led_6 (.in(ir_1_r));
  LED led_7 (.in(ir_1_w));
  LED led_8 (.in(registera_1_r));
  LED led_9 (.in(registera_1_w));
  // Probe on registera_1_alua
  RegisterA registera_1 (
    .DIN(rom_1_data), .LAL(LAL), .CLK(CLK), .LAH(LAH), .EA(EA), .DOUT(rom_1_data), .ALUA(registera_1_alua),
    .R(registera_1_r), .W(registera_1_w));
  Clock clock_1 (.out(clock_1_out));
  Multiplexer multiplexer_1 (.in0(clock_1_out), .in1(Pulse), .out(CLK), .sel(Manual));  // open: en

  // Other names for the same wires on the sheet: CLR = RESET

  // Notes on the sheet:
  //   Control Bus
  //   ISAP-1
  //   CPU
  //   MEMORY SUBSYSTEM
  //   Address Bus
  //   Address Reg
  //   PC
  //   IR
  //   Opcode
  //   CONTROL
  //   UNIT
  //   contents of rom_1 (hex, n*v repeats v):
  //   31 41 72 33 45 75 34 44 76 38 42 71 37 47 79 48
  //   Data Bus
  //   A
  //   CONTROL PANEL
endmodule

module RegisterA (
  input  [7:0] DIN,
  input  LAL,
  input  CLK,
  input  LAH,
  input  EA,
  output [7:0] ALUA,
  output [7:0] DOUT,
  output R,
  output W
);

  Register #(.width(4)) register_1 (.D(DIN[3:0]), .en(LAL), .Q(ALUA[3:0]), .clk(CLK));  // open: clr
  Register #(.width(4)) register_2 (.D(DIN[7:4]), .en(LAH), .Q(ALUA[7:4]), .clk(CLK));  // open: clr
  or or_1 (R, LAL, LAH);
  assign DOUT = EA ? ALUA : 8'bz;  // Controlled_Buffer controlled_buffer_1

  assign W = EA;
endmodule

module AddressRegister (
  input  [7:0] DIN,
  input  LAR,
  input  CLK,
  output [3:0] ABUS,
  output R
);

  Register #(.width(4)) register_1 (.D(DIN[3:0]), .en(LAR), .Q(ABUS), .clk(CLK));  // open: clr

  assign R = LAR;
endmodule

module PC (
  input  LP,
  input  [7:0] DIN,
  input  CP,
  input  CLK,
  input  CLR,
  input  EP,
  output [7:0] PROBE,
  output [7:0] DOUT,
  output W,
  output R
);

  // Probe on PROBE[3:0]
  Counter #(.width(4), .max('hf)) counter_1 (
    .load(LP), .D(DIN[3:0]), .count(CP), .Q(PROBE[3:0]), .clk(CLK), .clr(CLR));  // open: carry
  assign PROBE[7:4] = 4'b0000;  // Buffer buffer_1, 4 bits wide
  assign DOUT = EP ? PROBE : 8'bz;  // Controlled_Buffer controlled_buffer_1
  // Probe on PROBE[7:4]
  // Probe on DOUT

  assign R = LP;
  assign W = EP;
endmodule

module IR (
  input  [7:0] DIN,
  input  LI,
  input  CLK,
  input  CLR,
  input  EI,
  output [7:0] PROBE,
  output [7:0] DOUT,
  output [3:0] INSTR,
  output R,
  output W
);

  Register register_1 (.D(DIN), .en(LI), .Q({INSTR, PROBE[3:0]}), .clk(CLK), .clr(CLR));
  // Probe on PROBE[3:0]
  assign DOUT[3:0] = EI ? PROBE[3:0] : 4'bz;  // Controlled_Buffer controlled_buffer_1
  assign DOUT[7:4] = EI ? PROBE[3:0] : 4'bz;  // Controlled_Buffer controlled_buffer_2
  // Probe on DOUT[3:0]
  // Probe on DOUT[7:4]

  assign PROBE[7:4] = INSTR;
  assign R = LI;
  assign W = EI;
endmodule

module CONTROL (
  input  [3:0] INSTR,
  input  CLK,
  input  CLR,
  output [4:0] CTRL_W,
  output [5:0] CTRL_R,
  output CTRL
);

  wire and_1_out, and_2_out, and_3_out, and_4_out, and_5_out, and_6_out, and_7_out, and_8_out, and_9_out,
       and_10_out, and_11_out, and_12_out, and_13_out, and_14_out, and_15_out, and_16_out, and_17_out,
       and_18_out, and_19_out, and_20_out, decoder_1_out0, decoder_1_out1, decoder_1_out2, decoder_1_out3,
       decoder_1_out4, decoder_1_out5, decoder_1_out6, decoder_1_out7, decoder_1_out8, decoder_1_out9,
       decoder_1_out10, decoder_1_out11, decoder_1_out12, decoder_1_out13, decoder_1_out14, decoder_1_out15,
       decoder_2_out0, decoder_2_out1, decoder_2_out2, decoder_2_out3, decoder_2_out4, not_1_out, or_1_out,
       or_2_out;
  wire [2:0] counter_1_q;

  Decoder #(.select(4), .disabled(0), .enable("false")) decoder_1 (
    .out0(decoder_1_out0), .out1(decoder_1_out1), .out2(decoder_1_out2), .out3(decoder_1_out3),
    .out4(decoder_1_out4), .out5(decoder_1_out5), .out6(decoder_1_out6), .out7(decoder_1_out7),
    .out8(decoder_1_out8), .out9(decoder_1_out9), .out10(decoder_1_out10), .out11(decoder_1_out11),
    .out12(decoder_1_out12), .out13(decoder_1_out13), .out14(decoder_1_out14), .out15(decoder_1_out15),
    .sel(INSTR));
  not not_1 (not_1_out, CLK);
  // Probe on counter_1_q
  or or_1 (or_1_out, CLR, and_17_out, and_20_out, or_2_out, and_18_out);
  and and_1 (and_1_out, decoder_1_out0, decoder_2_out2);
  and and_2 (and_2_out, decoder_1_out1, decoder_2_out2);
  and and_3 (and_3_out, decoder_1_out2, decoder_2_out2);
  and and_4 (and_4_out, decoder_1_out3, decoder_2_out2);
  and and_5 (and_5_out, decoder_1_out4, decoder_2_out2);
  and and_6 (and_6_out, decoder_1_out5, decoder_2_out2);
  and and_7 (and_7_out, decoder_1_out6, decoder_2_out2);
  and and_8 (and_8_out, decoder_1_out7, decoder_2_out2);
  and and_9 (and_9_out, decoder_1_out8, decoder_2_out2);
  and and_10 (and_10_out, decoder_1_out9, decoder_2_out2);
  and and_11 (and_11_out, decoder_1_out10, decoder_2_out2);
  and and_12 (and_12_out, decoder_1_out11, decoder_2_out2);
  and and_13 (and_13_out, decoder_1_out12, decoder_2_out2);
  and and_14 (and_14_out, decoder_1_out13, decoder_2_out2);
  and and_15 (and_15_out, decoder_1_out14, decoder_2_out2);
  and and_16 (and_16_out, decoder_1_out15, decoder_2_out2);
  Decoder #(.select(3), .disabled(0), .enable("false")) decoder_2 (
    .out0(decoder_2_out0), .out1(decoder_2_out1), .out2(decoder_2_out2), .out3(decoder_2_out3),
    .out4(decoder_2_out4), .sel(counter_1_q));  // open: out5, out6, out7
  Counter #(.width(3), .max('h7)) counter_1 (
    .Q(counter_1_q), .clk(not_1_out), .clr(or_1_out));  // open: load, D, count, carry
  or or_2 (or_2_out, and_1_out, and_2_out, and_3_out, and_6_out, and_7_out, and_9_out, and_10_out, and_11_out, and_12_out, and_13_out, and_14_out, and_15_out, and_16_out);
  and and_17 (and_17_out, decoder_1_out3, decoder_2_out3);
  and and_18 (and_18_out, decoder_1_out4, decoder_2_out3);
  and and_19 (and_19_out, decoder_1_out7, decoder_2_out3);
  or or_3 (CTRL_W[2], and_4_out, and_8_out, and_5_out);
  buf buffer_1 (CTRL_W[1], decoder_2_out1);
  or or_4 (CTRL_R[0], decoder_2_out0, and_8_out);
  buf buffer_2 (CTRL_R[1], decoder_2_out1);
  buf buffer_3 (CTRL, decoder_2_out1);
  and and_20 (and_20_out, decoder_1_out7, decoder_2_out4);
  buf buffer_4 (CTRL_W[0], decoder_2_out0);
  buf buffer_5 (CTRL_W[3], and_19_out);
  buf buffer_6 (CTRL_W[4], 1'b0);
  buf buffer_7 (CTRL_R[3], and_4_out);
  buf buffer_8 (CTRL_R[4], and_5_out);
  buf buffer_9 (CTRL_R[5], and_19_out);

  assign CTRL_R[2] = 1'b0;

  // Notes on the sheet:
  //   LIL
  //   LIH
  //   STA
  //   Step Counter
  //   T3
  //   Step Decoder
  //   NEXT
  //   LIL * T3
  //   LIH * T3
  //   STA * T3
  //   T1
  //   T7
  //   NOP * T3
  //   T4
  //   LIL * T4
  //   T5
  //   LIH * T4
  //   STA * T4
  //   STA * T5
  //   EP
  //   PM
  //   EI
  //   EA
  //   DM
  //   LAR
  //   LI
  //   LP
  //   LAL
  //   LAH
  //   W
  //   CP
  //   EXTRA CONTROLS
  //   BUS WRITE
  //   BUS READ
endmodule

module RAMtest (
  input  [7:0] in_1,
  input  ENABLE,
  input  [3:0] in_3,
  input  SEL,
  input  LD,
  input  ERASE
);

  wire [7:0] controlled_buffer_1_out;

  assign controlled_buffer_1_out = ENABLE ? in_1 : 8'bz;  // Controlled_Buffer controlled_buffer_1
  RAM #(.addrWidth(4), .bus("asynch")) ram_1 (
    .addr(in_3), .data(controlled_buffer_1_out), .sel(SEL), .ld(LD), .clr(ERASE));
  // Probe on controlled_buffer_1_out
endmodule
