// Logisim project ISAP-1_v5.circ as structural Verilog: 7 circuits, main circuit main
module main (
  input  in_1,
  input  RESET,
  input  Manual,
  input  Pulse
);

  wire addressregister_1_r, and_1_out, CLK, clock_1_out, CP, DM, EA, EI, EP, ir_1_r, ir_1_w, LAH, LAL, LAR,
       LI, LP, not_1_out, not_2_out, not_3_out, pc_1_r, pc_1_w, PM, registera_1_r, registera_1_w, W;
  wire [3:0] addressregister_1_abus, ir_1_instr;
  wire [7:0] ir_1_probe, pc_1_probe, registera_1_alua, rom_1_data;

  not not_1 (not_1_out, W);
  and and_1 (and_1_out, not_1_out, DM);
  not not_2 (not_2_out, DM);
  not not_3 (not_3_out, not_2_out);
  // Probe on addressregister_1_abus
  // Probe on ir_1_instr
  CONTROL control_1 (
    .INSTR(ir_1_instr), .CTRL(CP), .CLK(CLK), .CLR(RESET), .CTRL_R({W, LAH, LAL, LP, LI, LAR}),
    .CTRL_W({DM, EA, EI, PM, EP}));
  ROM #(.addrWidth(4)) rom_1 (.addr(addressregister_1_abus), .data(rom_1_data), .sel(PM));
  RAM #(.addrWidth(4), .bus("asynch")) ram_1 (
    .addr(addressregister_1_abus), .data(rom_1_data), .sel(not_3_out), .ld(and_1_out), .clr(in_1));
  // Probe on addressregister_1_abus
  // Probe on pc_1_probe
  // Probe on pc_1_probe
  // Probe on ir_1_probe
  // Probe on ir_1_probe
  // Probe on ir_1_instr
  LED led_1 (.in(PM));
  LED led_2 (.in(not_3_out));
  LED led_3 (.in(addressregister_1_r));
  AddressRegister addressregister_1 (
    .DIN(rom_1_data), .LAR(LAR), .CLK(CLK), .ABUS(addressregister_1_abus), .R(addressregister_1_r));
  LED led_4 (.in(pc_1_r));
  PC pc_1 (
    .LP(LP), .DIN(rom_1_data), .CP(CP), .CLK(CLK), .CLR(RESET), .EP(EP), .DOUT(rom_1_data),
    .PROBE(pc_1_probe), .W(pc_1_w), .R(pc_1_r));
  LED led_5 (.in(pc_1_w));
  LED led_6 (.in(ir_1_r));
  IR ir_1 (
    .LI(LI), .CLK(CLK), .CLR(RESET), .EI(EI), .DOUT(rom_1_data), .INSTR(ir_1_instr), .PROBE(ir_1_probe),
    .DIN(rom_1_data), .R(ir_1_r), .W(ir_1_w));
  LED led_7 (.in(ir_1_w));
  // Probe on rom_1_data
  // Probe on rom_1_data
  LED led_8 (.in(registera_1_r));
  LED led_9 (.in(registera_1_w));
  // Probe on registera_1_alua
  // Probe on registera_1_alua
  RegisterA registera_1 (
    .DIN(rom_1_data), .LAL(LAL), .CLK(CLK), .LAH(LAH), .EA(EA), .DOUT(rom_1_data), .ALUA(registera_1_alua),
    .R(registera_1_r), .W(registera_1_w));
  Clock clock_1 (.out(clock_1_out));
  Multiplexer multiplexer_1 (.in0(clock_1_out), .in1(Pulse), .out(CLK), .sel(Manual));  // open: en

  // Other names for the same wires on the sheet: CLR = RESET

  // Notes on the sheet:
  //   ISAP-1
  //   CPU
  //   MEMORY SUBSYSTEM
  //   Control Bus
  //   Address Bus
  //   Opcode
  //   ROM
  //   contents of rom_1 (hex, n*v repeats v):
  //   31 41 70 0 75 5 7a a 7f f 73 3 76 6 79 7c
  //   RAM
  //   Address Reg
  //   PC
  //   IR
  //   CONTROL
  //   UNIT
  //   Data Bus
  //   A
  //   CONTROL PANEL
endmodule

module RegisterA (
  input  [7:0] DIN,
  input  LAL,
  input  CLK,
  input  LAH,
  input  EA,
  output [7:0] ALUA,
  output [7:0] DOUT,
  output R,
  output W
);

  Register #(.width(4)) register_1 (.D(DIN[3:0]), .en(LAL), .Q(ALUA[3:0]), .clk(CLK));  // open: clr
  Register #(.width(4)) register_2 (.D(DIN[7:4]), .en(LAH), .Q(ALUA[7:4]), .clk(CLK));  // open: clr
  or or_1 (R, LAL, LAH);
  assign DOUT = EA ? ALUA : 8'bz;  // Controlled_Buffer controlled_buffer_1

  assign W = EA;
endmodule

module AddressRegister (
  input  [7:0] DIN,
  input  LAR,
  input  CLK,
  output [3:0] ABUS,
  output R
);

  Register #(.width(4)) register_1 (.D(DIN[3:0]), .en(LAR), .Q(ABUS), .clk(CLK));  // open: clr

  assign R = LAR;
endmodule

module PC (
  input  LP,
  input  [7:0] DIN,
  input  CP,
  input  CLK,
  input  CLR,
  input  EP,
  output [7:0] PROBE,
  output [7:0] DOUT,
  output W,
  output R
);

  // Probe on PROBE[3:0]
  Counter #(.width(4), .max('hf)) counter_1 (
    .load(LP), .D(DIN[3:0]), .count(CP), .Q(PROBE[3:0]), .clk(CLK), .clr(CLR));  // open: carry
  assign PROBE[7:4] = 4'b0000;  // Buffer buffer_1, 4 bits wide
  assign DOUT = EP ? PROBE : 8'bz;  // Controlled_Buffer controlled_buffer_1
  // Probe on PROBE[7:4]
  // Probe on DOUT

  assign R = LP;
  assign W = EP;
endmodule

module IR (
  input  [7:0] DIN,
  input  LI,
  input  CLK,
  input  CLR,
  input  EI,
  output [7:0] PROBE,
  output [7:0] DOUT,
  output [3:0] INSTR,
  output R,
  output W
);

  Register register_1 (.D(DIN), .en(LI), .Q({INSTR, PROBE[3:0]}), .clk(CLK), .clr(CLR));
  // Probe on PROBE[3:0]
  assign DOUT[3:0] = EI ? PROBE[3:0] : 4'bz;  // Controlled_Buffer controlled_buffer_1
  assign DOUT[7:4] = EI ? PROBE[3:0] : 4'bz;  // Controlled_Buffer controlled_buffer_2
  // Probe on DOUT[3:0]
  // Probe on DOUT[7:4]

  assign PROBE[7:4] = INSTR;
  assign R = LI;
  assign W = EI;
endmodule

module CONTROL (
  input  [3:0] INSTR,
  input  CLK,
  input  CLR,
  output [4:0] CTRL_W,
  output [5:0] CTRL_R,
  output CTRL
);

  wire and_1_out, and_2_out, and_3_out, and_4_out, and_5_out, and_6_out, decoder_1_out0, decoder_1_out3,
       decoder_1_out4, decoder_1_out7, decoder_2_out0, decoder_2_out1, decoder_2_out2, decoder_2_out3,
       decoder_2_out4, not_1_out, or_1_out, or_3_out, or_5_out, or_6_out;
  wire [2:0] counter_1_q;

  Decoder #(.select(4), .disabled(0), .enable("false")) decoder_1 (
    .out0(decoder_1_out0), .out3(decoder_1_out3), .out4(decoder_1_out4), .out7(decoder_1_out7), .sel(INSTR));  // open: out1, out2, out5, out6, out8, out9, out10, out11, out12, out13, out14, out15
  not not_1 (not_1_out, CLK);
  // Probe on counter_1_q
  or or_1 (or_1_out, CLR, decoder_2_out4);
  Decoder #(.select(3), .disabled(0), .enable("false")) decoder_2 (
    .out0(decoder_2_out0), .out1(decoder_2_out1), .out2(decoder_2_out2), .out3(decoder_2_out3),
    .out4(decoder_2_out4), .sel(counter_1_q));  // open: out5, out6, out7
  Counter #(.width(3), .max('h7)) counter_1 (
    .Q(counter_1_q), .clk(not_1_out), .clr(or_1_out));  // open: load, D, count, carry
  and and_1 (and_1_out, decoder_1_out0, decoder_2_out2);
  and and_2 (and_2_out, decoder_1_out3, decoder_2_out2);
  and and_3 (and_3_out, decoder_1_out4, decoder_2_out2);
  and and_4 (and_4_out, decoder_1_out7, decoder_2_out2);
  and and_5 (and_5_out, decoder_1_out0, decoder_2_out3);
  and and_6 (and_6_out, decoder_1_out7, decoder_2_out3);
  or or_2 (CTRL_W[2], and_1_out, and_2_out, and_3_out, and_4_out);
  or or_3 (or_3_out, and_6_out, and_5_out);
  or or_4 (CTRL_R[0], decoder_2_out0, and_1_out, and_4_out);
  or or_5 (or_5_out, and_5_out, and_2_out);
  or or_6 (or_6_out, and_5_out, and_3_out);
  buf buffer_1 (CTRL, decoder_2_out1);
  buf buffer_2 (CTRL_W[0], decoder_2_out0);
  buf buffer_3 (CTRL_W[1], decoder_2_out1);
  buf buffer_4 (CTRL_W[3], and_6_out);
  buf buffer_5 (CTRL_W[4], or_3_out);
  buf buffer_6 (CTRL_R[1], decoder_2_out1);
  buf buffer_7 (CTRL_R[3], or_5_out);
  buf buffer_8 (CTRL_R[4], or_6_out);
  buf buffer_9 (CTRL_R[5], and_6_out);

  assign CTRL_R[2] = 1'b0;

  // Notes on the sheet:
  //   LDA
  //   LIL
  //   LIH
  //   STA
  //   Step Counter
  //   T3
  //   Step Decoder
  //   NEXT
  //   LDA * T3
  //   LIL * T3
  //   LIH * T3
  //   STA * T3
  //   T1
  //   T7
  //   T4
  //   LDA * T4
  //   STA * T4
  //   EP
  //   PM
  //   EI
  //   EA
  //   DM
  //   LAR
  //   LI
  //   LP
  //   LAL
  //   CP
  //   LAH
  //   W
  //   EXTRA CONTROLS
  //   BUS WRITE
  //   BUS READ
endmodule

module RAMtest (
  input  [7:0] in_1,
  input  ENABLE,
  input  [3:0] in_3,
  input  SEL,
  input  LD,
  input  ERASE,
  input  [7:0] in_7,
  input  ENABLE_2,
  input  [3:0] in_9,
  input  DM,
  input  W,
  input  ERASE_2
);

  wire and_1_out, not_1_out, not_2_out, not_3_out;
  wire [7:0] controlled_buffer_1_out, controlled_buffer_2_out;

  and and_1 (and_1_out, DM, not_1_out);
  not not_1 (not_1_out, W);
  not not_2 (not_2_out, DM);
  not not_3 (not_3_out, not_2_out);
  assign controlled_buffer_1_out = ENABLE ? in_1 : 8'bz;  // Controlled_Buffer controlled_buffer_1
  assign controlled_buffer_2_out = ENABLE_2 ? in_7 : 8'bz;  // Controlled_Buffer controlled_buffer_2
  RAM #(.addrWidth(4), .bus("asynch")) ram_1 (
    .addr(in_3), .data(controlled_buffer_1_out), .sel(SEL), .ld(LD), .clr(ERASE));
  // Probe on controlled_buffer_1_out
  RAM #(.addrWidth(4), .bus("asynch")) ram_2 (
    .addr(in_9), .data(controlled_buffer_2_out), .sel(not_3_out), .ld(and_1_out), .clr(ERASE_2));
  // Probe on controlled_buffer_2_out
endmodule
