// Logisim project ISAP-1_ver0_1.circ as structural Verilog: 5 circuits, main circuit main
module main (
  input  RESET,
  input  Manual,
  input  Pulse
);

  wire addressregister_1_r, CLK, clock_1_out, CP, EP, ir_1_r, LAR, LI, not_1_out, pc_1_w;
  wire [3:0] addressregister_1_abus, ir_1_instr, pc_1_probe;
  wire [7:0] ir_1_probe, pc_1_dout;

  not not_1 (not_1_out, not_1_out);
  LED led_1 (.in(CP));
  // Probe on addressregister_1_abus
  // Probe on ir_1_instr
  // Probe on addressregister_1_abus
  // Probe on pc_1_probe
  // Probe on pc_1_probe
  // Probe on ir_1_probe
  // Probe on ir_1_probe
  // Probe on ir_1_instr
  // Probe on pc_1_dout
  LED led_2 (.in(addressregister_1_r));
  AddressRegister addressregister_1 (
    .DIN(pc_1_dout), .LAR(LAR), .CLK(CLK), .ABUS(addressregister_1_abus), .R(addressregister_1_r));
  PC pc_1 (.CP(CP), .CLK(CLK), .CLR(RESET), .EP(EP), .DOUT(pc_1_dout), .PROBE(pc_1_probe), .W(pc_1_w));
  LED led_3 (.in(pc_1_w));
  LED led_4 (.in(ir_1_r));
  IR ir_1 (.LI(LI), .CLK(CLK), .CLR(RESET), .INSTR(ir_1_instr), .PROBE(ir_1_probe), .DIN(pc_1_dout), .R(ir_1_r));
  CONTROL control_1 (.INSTR(ir_1_instr), .CLK(CLK), .CLR(RESET), .CTRL({LI, LAR, EP, CP}));
  // Probe on pc_1_dout
  Clock clock_1 (.out(clock_1_out));
  Multiplexer #(.disabled(0), .enable("false")) multiplexer_1 (.in0(clock_1_out), .in1(Pulse), .out(CLK), .sel(Manual));

  // Other names for the same wires on the sheet: CLR = RESET

  // Notes on the sheet:
  //   ISAP-1
  //   CPU
  //   Address Bus
  //   4 bit
  //   Opcode
  //   Address Reg
  //   PC
  //   IR
  //   CONTROL
  //   UNIT
  //   Data Bus
  //   8 bit
  //   ISAP-1   COMPUTER   Version 0.1
  //   CONTROL   PANEL
  //   Control Bus
  //   2 bit
  //   in
  //   in
endmodule

module AddressRegister (
  input  [7:0] DIN,
  input  LAR,
  input  CLK,
  output [3:0] ABUS,
  output R
);

  Register #(.width(4)) register_1 (.D(DIN[3:0]), .en(LAR), .Q(ABUS), .clk(CLK));  // open: clr

  assign R = LAR;

  // Notes on the sheet:
  //   4 bit Register
  //   ADDRESS REGISTER
endmodule

module PC (
  input  CP,
  input  CLK,
  input  CLR,
  input  EP,
  output [3:0] PROBE,
  output [7:0] DOUT,
  output W
);

  wire j_k_ff_1_qn, j_k_ff_2_qn, j_k_ff_3_qn, j_k_ff_4_qn;

  J_K_Flip_Flop j_k_ff_1 (.J(CP), .clk(CLK), .K(CP), .Q(PROBE[0]), .Qn(j_k_ff_1_qn), .reset(CLR));  // open: preset, en
  assign DOUT[0] = EP ? PROBE[0] : 1'bz;  // Controlled_Buffer controlled_buffer_1
  J_K_Flip_Flop j_k_ff_2 (
    .J(CP), .clk(j_k_ff_1_qn), .K(CP), .Q(PROBE[1]), .Qn(j_k_ff_2_qn), .reset(CLR));  // open: preset, en
  assign DOUT[1] = EP ? PROBE[1] : 1'bz;  // Controlled_Buffer controlled_buffer_2
  J_K_Flip_Flop j_k_ff_3 (
    .J(CP), .clk(j_k_ff_2_qn), .K(CP), .Q(PROBE[2]), .Qn(j_k_ff_3_qn), .reset(CLR));  // open: preset, en
  assign DOUT[2] = EP ? PROBE[2] : 1'bz;  // Controlled_Buffer controlled_buffer_3
  J_K_Flip_Flop j_k_ff_4 (
    .J(CP), .clk(j_k_ff_3_qn), .K(CP), .Q(PROBE[3]), .Qn(j_k_ff_4_qn), .reset(CLR));  // open: preset, en
  assign DOUT[3] = EP ? PROBE[3] : 1'bz;  // Controlled_Buffer controlled_buffer_4
  assign DOUT[7] = EP ? 1'b1 : 1'bz;  // Controlled_Buffer controlled_buffer_5

  assign DOUT[6:4] = {3{DOUT[7]}};
  assign W = EP;

  // Notes on the sheet:
  //   4 x JK Flip-Flop
  //   4 bit Buffer
  //   PROGRAM  COUNTER
endmodule

module IR (
  input  [7:0] DIN,
  input  LI,
  input  CLK,
  input  CLR,
  output [7:0] PROBE,
  output [3:0] INSTR,
  output R
);

  Register register_1 (.D(DIN), .en(LI), .Q({INSTR, PROBE[3:0]}), .clk(CLK), .clr(CLR));

  assign PROBE[7:4] = INSTR;
  assign R = LI;

  // Notes on the sheet:
  //   8 bit Register
  //   INSTRUCTION  REGISTER
endmodule

module CONTROL (
  input  CLK,
  input  CLR,
  input  [3:0] INSTR,
  output [3:0] CTRL
);

  wire j_k_ff_1_q, j_k_ff_1_qn, j_k_ff_2_q, j_k_ff_2_qn, j_k_ff_3_q, j_k_ff_3_qn, j_k_ff_4_q, j_k_ff_4_qn,
       j_k_ff_5_q, j_k_ff_5_qn, j_k_ff_6_q, j_k_ff_6_qn, not_1_out;

  not not_1 (not_1_out, CLK);
  buf buffer_1 (CTRL[1], j_k_ff_1_qn);
  buf buffer_2 (CTRL[0], j_k_ff_2_q);
  buf buffer_3 (CTRL[2], j_k_ff_1_qn);
  J_K_Flip_Flop j_k_ff_1 (
    .J(j_k_ff_6_qn), .clk(not_1_out), .K(j_k_ff_6_q), .Q(j_k_ff_1_q), .Qn(j_k_ff_1_qn), .reset(CLR));  // open: preset, en
  J_K_Flip_Flop j_k_ff_2 (
    .J(j_k_ff_1_qn), .clk(not_1_out), .K(j_k_ff_1_q), .Q(j_k_ff_2_q), .Qn(j_k_ff_2_qn), .reset(CLR));  // open: preset, en
  buf buffer_4 (CTRL[3], j_k_ff_3_q);
  J_K_Flip_Flop j_k_ff_3 (
    .J(j_k_ff_2_q), .clk(not_1_out), .K(j_k_ff_2_qn), .Q(j_k_ff_3_q), .Qn(j_k_ff_3_qn), .reset(CLR));  // open: preset, en
  J_K_Flip_Flop j_k_ff_4 (
    .J(j_k_ff_3_q), .clk(not_1_out), .K(j_k_ff_3_qn), .Q(j_k_ff_4_q), .Qn(j_k_ff_4_qn), .reset(CLR));  // open: preset, en
  J_K_Flip_Flop j_k_ff_5 (
    .J(j_k_ff_4_q), .clk(not_1_out), .K(j_k_ff_4_qn), .Q(j_k_ff_5_q), .Qn(j_k_ff_5_qn), .reset(CLR));  // open: preset, en
  J_K_Flip_Flop j_k_ff_6 (
    .J(j_k_ff_5_q), .clk(not_1_out), .K(j_k_ff_5_qn), .Q(j_k_ff_6_q), .Qn(j_k_ff_6_qn), .reset(CLR));  // open: preset, en

  // Notes on the sheet:
  //   EP
  //   CP
  //   LAR
  //   CONTROL    MATRIX
  //   CONTROL    UNIT
  //   T1
  //   T2
  //   LI
  //   RING COUNTER
  //   T3
  //   T4
  //   T5
  //   T6
endmodule
